# Fritzing sketch garden_sensor (saved by Fritzing 0.9.4)
breadboards: 1

parts:
  U2 = ESP32S-HiLetgo [part_number=ESP32S-HiLetgo]
  Capacitive_Soil_Moisture_Sensor = Soil Moisture Sensor
  5v_dc = Battery Holders [package=battcon_12mm]
  U3 = RELAY-2 [package=relay-g5v]
  5v_optoisolated_relay_module = Sharp PC817 [package=THT]
  12v_Water_solenoid_valve = Solenoid
  12v_dc = Battery Holders [package=battcon_12mm]

nets:
  N1: U2.GPIO32, Capacitive_Soil_Moisture_Sensor.SIG
  GND: U2.GND, Capacitive_Soil_Moisture_Sensor.GND, 5v_dc.+, U3.9
  VIN: U2.VIN, Capacitive_Soil_Moisture_Sensor.VCC, 5v_dc.-, 5v_optoisolated_relay_module.Pin_3
  N2: U2.GPIO2, 5v_optoisolated_relay_module.Pin_1
  N3: U3.2, 5v_optoisolated_relay_module.Pin_4
  N4: U3.6, 12v_dc.+
  N5: U3.10, 12v_Water_solenoid_valve.pin1
  N6: 12v_Water_solenoid_valve.pin2, 12v_dc.-

notes:
  5v optoisolated relay module

custom parts:
  ESP32S-HiLetgo: HiLetgo ESP-WROOM-32 ESP32 ESP-32S Development Board 2.4GHz Dual-Mode WiFi + Bluetooth Dual Cores Microcontroller The ESP32 integrated with Antenna switches, RF Balun, power amplifiers, low-noise amplifiers, filters, and management modules, and the entire solution occupies the least area of PCB. 2.4 GHz Wi-Fi plus Bluetooth dual-mode chip, with TSMC Ultra-low power consumption 40nm technology,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
